# Fritzing sketch Nokia5110LM35 (saved by Fritzing 0.9.2b)
breadboards: 1

parts:
  Nokia_5110_LCD_Module1 = Nokia5110LCDModule
  Eleman1 = Arduino Uno (Rev3)
  T1 = LM35 Temperature Sensor [package="TO92 [THT]"]

nets:
  N1: Nokia_5110_LCD_Module1.Vcc, Eleman1.D11_PWM/MOSI
  N2: Nokia_5110_LCD_Module1.Grnd, Eleman1.D12/MISO
  N3: Nokia_5110_LCD_Module1.SCE, Eleman1.D10_PWM/SS
  N4: Nokia_5110_LCD_Module1.RST, Eleman1.D9_PWM
  N5: Nokia_5110_LCD_Module1.D/C, Eleman1.D8
  N6: Nokia_5110_LCD_Module1.6_DN_(MOSI), Eleman1.5V
  N7: Nokia_5110_LCD_Module1.SCLK, Eleman1.D7
  GND: Nokia_5110_LCD_Module1.LED, Eleman1.GND, T1.GND
  N8: Eleman1.A0, T1.Vout

custom parts:
  : Nokia 5110 LCD with 8 pin. It's a 45mm*45mm module part. Description: The Nokia 5110 is a basic graphic LCD screen for lots of applications. It was originally intended for as a cell phone screen. This one is mounted on an easy to solder PCB. It uses the PCD8544 controller. The PCD8544 is a low power CMOS LCD controller/driver, designed to drive a graphic display of 48 rows and 84 columns. All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
